// Logisim project control-logic.circ as structural Verilog: 1 circuit, main circuit control_logic
module control_logic (
  input  [31:0] Instruction,
  input  BrEq,
  input  BrLt,
  output PCSel,
  output RegWEn,
  output [2:0] ImmSel,
  output BrUn,
  output ASel,
  output BSel,
  output [3:0] ALUSel,
  output MemWEn,
  output [1:0] WBSel
);

  wire and_1_out, and_2_out, and_3_out, and_4_out, and_5_out, comparator_1_eq, comparator_2_eq,
       comparator_3_eq, comparator_4_eq, comparator_5_eq, comparator_6_eq, comparator_7_eq, comparator_8_eq,
       comparator_9_gt, comparator_10_eq, comparator_11_eq, comparator_12_eq, comparator_13_eq,
       comparator_14_eq, comparator_15_eq, comparator_16_eq, comparator_17_eq, comparator_18_eq,
       comparator_19_eq, comparator_20_eq, comparator_21_eq, comparator_22_eq, comparator_23_eq,
       comparator_24_eq, not_1_out, not_2_out, or_1_out, or_2_out, or_3_out;
  wire [5:0] adder_1_out, adder_2_out, adder_3_out, adder_4_out, adder_5_out, bit_extender_1_out,
       bit_extender_2_out, bit_extender_3_out, bit_extender_4_out, bit_extender_5_out, bit_extender_6_out,
       inp, multiplexer_1_out, multiplexer_2_out, multiplexer_3_out, multiplexer_4_out, multiplexer_5_out,
       multiplexer_6_out, multiplexer_7_out, multiplexer_8_out, multiplexer_9_out, multiplexer_10_out,
       multiplexer_11_out, multiplexer_12_out, multiplexer_13_out, multiplexer_14_out, multiplexer_16_out;
  wire [15:14] rom_1_data;

  ROM #(.addrWidth(6), .dataWidth(16)) rom_1 (
    .addr(inp), .data({rom_1_data, WBSel, MemWEn, ALUSel, BSel, ASel, BrUn, ImmSel, RegWEn}));
  Comparator #(.mode("unsigned"), .width(7)) comparator_1 (
    .a(Instruction[31:25]), .b({7{1'b0}}), .eq(comparator_1_eq));  // open: gt, lt
  Bit_Extender #(.in_width(7), .out_width(6), .\type ("zero")) bit_extender_1 (
    .in(Instruction[31:25]), .out(bit_extender_1_out));
  Comparator #(.mode("unsigned"), .width(7)) comparator_2 (
    .a(Instruction[31:25]), .b(7'b0100000), .eq(comparator_2_eq));  // open: gt, lt
  Bit_Extender #(.in_width(7), .out_width(6), .\type ("zero")) bit_extender_2 (
    .in(Instruction[31:25]), .out(bit_extender_2_out));
  Adder #(.width(6)) adder_1 (.a(bit_extender_2_out), .b(6'b000011), .out(adder_1_out));  // open: cin, cout
  Multiplexer #(.width(6)) multiplexer_1 (
    .in0(6'b001001), .in1(6'b001000), .out(multiplexer_1_out), .sel(comparator_1_eq));
  Multiplexer #(.width(6)) multiplexer_2 (
    .in0(bit_extender_1_out), .in1(6'b000010), .out(multiplexer_2_out), .sel(comparator_2_eq));
  Multiplexer #(.select(3), .width(6)) multiplexer_3 (
    .in0(multiplexer_2_out), .in1(adder_1_out), .in2(6'b000110), .in3(6'b000101), .in4(6'b000111),
    .in5(multiplexer_1_out), .in6(6'b001010), .in7(6'b001011), .out(multiplexer_3_out),
    .sel(Instruction[14:12]));
  Comparator #(.mode("unsigned"), .width(7)) comparator_3 (
    .a(Instruction[6:0]), .b(7'b0110011), .eq(comparator_3_eq));  // open: gt, lt
  assign bit_extender_3_out = {{3{1'b0}}, Instruction[14:12]};  // Bit_Extender bit_extender_3
  Multiplexer #(.width(6)) multiplexer_4 (
    .in0(6'b010100), .in1(6'b010011), .out(multiplexer_4_out), .sel(comparator_4_eq));
  Comparator #(.mode("unsigned"), .width(7)) comparator_4 (
    .a(Instruction[31:25]), .b({7{1'b0}}), .eq(comparator_4_eq));  // open: gt, lt
  Comparator #(.width(3)) comparator_5 (.a(Instruction[14:12]), .b(3'b110), .eq(comparator_5_eq));  // open: gt, lt
  Comparator #(.width(3)) comparator_6 (.a(Instruction[14:12]), .b(3'b100), .eq(comparator_6_eq));  // open: gt, lt
  Comparator #(.width(3)) comparator_7 (.a(Instruction[14:12]), .b(3'b101), .eq(comparator_7_eq));  // open: gt, lt
  Comparator #(.width(3)) comparator_8 (.a(Instruction[14:12]), .b(3'b111), .eq(comparator_8_eq));  // open: gt, lt
  Adder #(.width(6)) adder_2 (.a(6'b010111), .b(bit_extender_3_out), .out(adder_2_out));  // open: cin, cout
  Adder #(.width(6)) adder_3 (.a(6'b001100), .b(bit_extender_4_out), .out(adder_3_out));  // open: cin, cout
  assign bit_extender_4_out = {{3{1'b0}}, Instruction[14:12]};  // Bit_Extender bit_extender_4
  Comparator #(.mode("unsigned"), .width(3)) comparator_9 (
    .a(Instruction[14:12]), .b(3'b010), .gt(comparator_9_gt));  // open: eq, lt
  assign bit_extender_5_out = {{3{1'b0}}, Instruction[14:12]};  // Bit_Extender bit_extender_5
  Comparator #(.mode("unsigned"), .width(3)) comparator_10 (
    .a(Instruction[14:12]), .b(3'b101), .eq(comparator_10_eq));  // open: gt, lt
  Comparator #(.width(3)) comparator_11 (.a(Instruction[14:12]), .b(3'b000), .eq(comparator_11_eq));  // open: gt, lt
  Comparator #(.width(3)) comparator_12 (.a(Instruction[14:12]), .b(3'b001), .eq(comparator_12_eq));  // open: gt, lt
  not not_1 (not_1_out, BrEq);
  or or_1 (or_1_out, comparator_5_eq, comparator_6_eq);
  or or_2 (or_2_out, comparator_7_eq, comparator_8_eq);
  not not_2 (not_2_out, BrLt);
  Multiplexer #(.width(6)) multiplexer_5 (
    .in1(6'b100000), .out(multiplexer_5_out), .sel(comparator_13_eq));  // open: in0
  Comparator #(.mode("unsigned"), .width(7)) comparator_13 (
    .a(Instruction[6:0]), .b(7'b0010111), .eq(comparator_13_eq));  // open: gt, lt
  Comparator #(.mode("unsigned"), .width(7)) comparator_14 (
    .a(Instruction[6:0]), .b(7'b0110111), .eq(comparator_14_eq));  // open: gt, lt
  Multiplexer #(.width(6)) multiplexer_6 (
    .in0(6'b011010), .in1(6'b011000), .out(multiplexer_6_out), .sel(comparator_9_gt));
  assign bit_extender_6_out = {{3{1'b0}}, Instruction[14:12]};  // Bit_Extender bit_extender_6
  and and_1 (and_1_out, comparator_11_eq, BrEq);
  and and_2 (and_2_out, comparator_12_eq, not_1_out);
  and and_3 (and_3_out, or_1_out, BrLt);
  and and_4 (and_4_out, or_2_out, not_2_out);
  Multiplexer #(.width(6)) multiplexer_7 (
    .in0(multiplexer_5_out), .in1(6'b100001), .out(multiplexer_7_out), .sel(comparator_14_eq));
  Multiplexer #(.width(6)) multiplexer_8 (
    .in0(multiplexer_7_out), .in1(6'b100010), .out(multiplexer_8_out), .sel(comparator_15_eq));
  Comparator #(.mode("unsigned"), .width(7)) comparator_15 (
    .a(Instruction[6:0]), .b(7'b1101111), .eq(comparator_15_eq));  // open: gt, lt
  Comparator #(.mode("unsigned"), .width(7)) comparator_16 (
    .a(Instruction[6:0]), .b(7'b0100011), .eq(comparator_16_eq));  // open: gt, lt
  Comparator #(.mode("unsigned"), .width(7)) comparator_17 (
    .a(Instruction[6:0]), .b(7'b0000011), .eq(comparator_17_eq));  // open: gt, lt
  Adder #(.width(6)) adder_4 (.a(multiplexer_6_out), .b(bit_extender_6_out), .out(adder_4_out));  // open: cin, cout
  Comparator #(.mode("unsigned"), .width(7)) comparator_18 (
    .a(Instruction[6:0]), .b(7'b1100011), .eq(comparator_18_eq));  // open: gt, lt
  Adder #(.width(6)) adder_5 (.a(6'b001111), .b(bit_extender_5_out), .out(adder_5_out));  // open: cin, cout
  Comparator #(.mode("unsigned"), .width(3)) comparator_19 (
    .a(Instruction[14:12]), .b(3'b100), .eq(comparator_19_eq));  // open: gt, lt
  Multiplexer #(.width(6)) multiplexer_9 (
    .in0(multiplexer_8_out), .in1(adder_2_out), .out(multiplexer_9_out), .sel(comparator_16_eq));
  Multiplexer #(.width(6)) multiplexer_10 (
    .in0(multiplexer_9_out), .in1(adder_3_out), .out(multiplexer_10_out), .sel(comparator_17_eq));
  Multiplexer #(.width(6)) multiplexer_11 (
    .in0(multiplexer_10_out), .in1(6'b100011), .out(multiplexer_11_out), .sel(comparator_20_eq));
  Comparator #(.mode("unsigned"), .width(7)) comparator_20 (
    .a(Instruction[6:0]), .b(7'b1100111), .eq(comparator_20_eq));  // open: gt, lt
  Multiplexer #(.width(6)) multiplexer_12 (
    .in0(adder_5_out), .in1(6'b010010), .out(multiplexer_12_out), .sel(comparator_19_eq));
  Comparator #(.mode("unsigned"), .width(7)) comparator_21 (
    .a(Instruction[6:0]), .b(7'b0010011), .eq(comparator_21_eq));  // open: gt, lt
  Comparator #(.width(7)) comparator_22 (.a(Instruction[6:0]), .b(7'b1101111), .eq(comparator_22_eq));  // open: gt, lt
  Comparator #(.width(7)) comparator_23 (.a(Instruction[6:0]), .b(7'b1100111), .eq(comparator_23_eq));  // open: gt, lt
  Comparator #(.width(7)) comparator_24 (.a(Instruction[6:0]), .b(7'b1100011), .eq(comparator_24_eq));  // open: gt, lt
  or or_3 (or_3_out, and_1_out, and_2_out, and_3_out, and_4_out);
  Multiplexer #(.width(6)) multiplexer_13 (
    .in0(multiplexer_11_out), .in1(adder_4_out), .out(multiplexer_13_out), .sel(comparator_18_eq));
  Multiplexer #(.width(6)) multiplexer_14 (
    .in0(multiplexer_13_out), .in1(multiplexer_3_out), .out(multiplexer_14_out), .sel(comparator_3_eq));
  Multiplexer #(.width(6)) multiplexer_15 (
    .in0(multiplexer_14_out), .in1(multiplexer_16_out), .out(inp), .sel(comparator_21_eq));
  Multiplexer #(.width(6)) multiplexer_16 (
    .in0(multiplexer_12_out), .in1(multiplexer_4_out), .out(multiplexer_16_out), .sel(comparator_10_eq));
  and and_5 (and_5_out, comparator_24_eq, or_3_out);
  or or_4 (PCSel, comparator_22_eq, comparator_23_eq, and_5_out);

  // Other names for the same wires on the sheet: opcode[6:0] = Instruction[6:0]; funct3[2:0] = Instruction[14:12];
  //   funct7[6:0] = Instruction[31:25]

  // Notes on the sheet:
  //   INPUTS to your circuit
  //   contents of rom_1 (hex, n*v repeats v):
  //   100f 140f 160f 108f 148f 158f 110f 120f 128f 168f 130f 138f 2041 2041 2041 1041 10c1 1141 1241 12c1
  //   16c1 1341 13c1 1842 1842 1842 4*1064 1074 1074 1067 17e7 3069 3041
  //   ROM FOR CONTROL LOGIC
  //   DON'T CHANGE THE LOCATIONS OF THE INPUTS AND OUTPUTS!
  //   This is only if you choose to do the ROM option
  //   CONNECT
  //   WIRE
  //   TO
  //   USE
  //   ROM
  //   OUTPUT from your circuit
  //   Reminder: If using ROM, use combinational logic for PCSel
endmodule
