// Logisim project imm-gen.circ as structural Verilog: 1 circuit, main circuit imm_gen
module imm_gen (
  input  [31:0] Instruction,
  input  [2:0] ImmSel,
  output [31:0] Immediate
);

  wire and_1_out, comparator_1_eq, comparator_2_eq, comparator_3_eq, or_1_out;
  wire [21:20] bit_extender_6_out;
  wire [31:0] bit_extender_3_out, bit_extender_4_out, bit_extender_5_out, I, Istar, multiplexer_1_out;

  assign I = {{20{Instruction[31]}}, Instruction[31:20]};  // Bit_Extender bit_extender_1
  assign Istar = {{27{Instruction[24]}}, Instruction[24:20]};  // Bit_Extender bit_extender_2
  Comparator #(.width(3)) comparator_1 (.a(3'b001), .b(Instruction[14:12]), .eq(comparator_1_eq));  // open: gt, lt
  Comparator #(.width(3)) comparator_2 (.a(Instruction[14:12]), .b(3'b101), .eq(comparator_2_eq));  // open: gt, lt
  Comparator #(.width(7)) comparator_3 (.a(Instruction[6:0]), .b(7'b0010011), .eq(comparator_3_eq));  // open: gt, lt
  assign bit_extender_3_out = {{20{Instruction[31]}}, {Instruction[31:25], Instruction[11:7]}};  // Bit_Extender bit_extender_3
  or or_1 (or_1_out, comparator_1_eq, comparator_2_eq);
  Multiplexer #(.width(32)) multiplexer_1 (.in0(I), .in1(Istar), .out(multiplexer_1_out), .sel(and_1_out));
  and and_1 (and_1_out, or_1_out, comparator_3_eq);
  assign bit_extender_4_out = {{19{Instruction[31]}}, {Instruction[31], Instruction[7], Instruction[30:25], Instruction[11:8], 1'b0}};  // Bit_Extender bit_extender_4
  assign bit_extender_5_out = {{10{bit_extender_6_out[21]}}, {bit_extender_6_out, Instruction[19:12], Instruction[20], Instruction[30:21], 1'b0}};  // Bit_Extender bit_extender_5
  assign bit_extender_6_out = {{1{Instruction[31]}}, Instruction[31]};  // Bit_Extender bit_extender_6
  Multiplexer #(.select(3), .width(32)) multiplexer_2 (
    .in0(multiplexer_1_out), .in1(bit_extender_3_out), .in2(bit_extender_4_out),
    .in3({Instruction[31:12], {12{1'b0}}}), .in4(bit_extender_5_out), .out(Immediate), .sel(ImmSel));  // open: in5, in6, in7

  // Other names for the same wires on the sheet: funct7[6:0] = Instruction[31:25]; funct3[2:0] = Instruction[14:12];
  //   opcode[6:0] = Instruction[6:0]

  // Notes on the sheet:
  //   INPUTS to your circuit
  //   DON'T CHANGE THE LOCATIONS OF THE INPUTS AND OUTPUTS!
  //   OUTPUT from your circuit
endmodule
