// Logisim project regfile.circ as structural Verilog: 1 circuit, main circuit regfile
module regfile (
  input  [4:0] ReadIndex1,
  input  [4:0] ReadIndex2,
  input  [4:0] WriteIndex,
  input  [31:0] WriteData,
  input  RegWEn,
  input  clk,
  output [31:0] ra,
  output [31:0] sp,
  output [31:0] t0,
  output [31:0] t1,
  output [31:0] t2,
  output [31:0] s0,
  output [31:0] s1,
  output [31:0] a0,
  output [31:0] ReadData1,
  output [31:0] ReadData2
);

  wire clock_1_out, clock_2_out, clock_3_out, clock_4_out, clock_5_out, clock_6_out, clock_7_out,
       clock_8_out, clock_9_out, clock_10_out, clock_11_out, clock_12_out, clock_13_out, clock_14_out,
       clock_15_out, clock_16_out, clock_17_out, clock_18_out, clock_19_out, clock_20_out, clock_21_out,
       clock_22_out, clock_23_out, clock_24_out, clock_25_out, clock_26_out, clock_27_out, clock_28_out,
       clock_29_out, clock_30_out, clock_31_out, demultiplexer_1_out1, demultiplexer_1_out2,
       demultiplexer_1_out3, demultiplexer_1_out4, demultiplexer_1_out5, demultiplexer_1_out6,
       demultiplexer_1_out7, demultiplexer_1_out8, demultiplexer_1_out9, demultiplexer_1_out10,
       demultiplexer_1_out11, demultiplexer_1_out12, demultiplexer_1_out13, demultiplexer_1_out14,
       demultiplexer_1_out15, demultiplexer_1_out16, demultiplexer_1_out17, demultiplexer_1_out18,
       demultiplexer_1_out19, demultiplexer_1_out20, demultiplexer_1_out21, demultiplexer_1_out22,
       demultiplexer_1_out23, demultiplexer_1_out24, demultiplexer_1_out25, demultiplexer_1_out26,
       demultiplexer_1_out27, demultiplexer_1_out28, demultiplexer_1_out29, demultiplexer_1_out30,
       demultiplexer_1_out31;
  wire [31:0] register_9_q, register_10_q, register_11_q, register_12_q, register_13_q, register_14_q,
       register_15_q, register_16_q, register_17_q, register_18_q, register_19_q, register_20_q,
       register_21_q, register_22_q, register_23_q, register_24_q, register_25_q, register_26_q,
       register_27_q, register_28_q, register_29_q, register_30_q, register_31_q;

  Register #(.width(32)) register_1 (.D(WriteData), .en(demultiplexer_1_out1), .clk(clock_1_out), .Q(ra));  // open: clr
  Clock clock_1 (.out(clock_1_out));
  Register #(.width(32)) register_2 (.D(WriteData), .en(demultiplexer_1_out2), .clk(clock_2_out), .Q(sp));  // open: clr
  Clock clock_2 (.out(clock_2_out));
  Register #(.width(32)) register_3 (.D(WriteData), .en(demultiplexer_1_out5), .clk(clock_3_out), .Q(t0));  // open: clr
  Clock clock_3 (.out(clock_3_out));
  Register #(.width(32)) register_4 (.D(WriteData), .en(demultiplexer_1_out6), .clk(clock_4_out), .Q(t1));  // open: clr
  Clock clock_4 (.out(clock_4_out));
  Register #(.width(32)) register_5 (.D(WriteData), .en(demultiplexer_1_out7), .clk(clock_5_out), .Q(t2));  // open: clr
  Clock clock_5 (.out(clock_5_out));
  Register #(.width(32)) register_6 (.D(WriteData), .en(demultiplexer_1_out8), .clk(clock_6_out), .Q(s0));  // open: clr
  Clock clock_6 (.out(clock_6_out));
  Register #(.width(32)) register_7 (.D(WriteData), .en(demultiplexer_1_out9), .clk(clock_7_out), .Q(s1));  // open: clr
  Clock clock_7 (.out(clock_7_out));
  Register #(.width(32)) register_8 (
    .D(WriteData), .en(demultiplexer_1_out10), .clk(clock_8_out), .Q(a0));  // open: clr
  Clock clock_8 (.out(clock_8_out));
  Demultiplexer #(.select(5)) demultiplexer_1 (
    .out1(demultiplexer_1_out1), .out2(demultiplexer_1_out2), .out3(demultiplexer_1_out3),
    .out4(demultiplexer_1_out4), .out5(demultiplexer_1_out5), .out6(demultiplexer_1_out6),
    .out7(demultiplexer_1_out7), .out8(demultiplexer_1_out8), .out9(demultiplexer_1_out9),
    .out10(demultiplexer_1_out10), .out11(demultiplexer_1_out11), .out12(demultiplexer_1_out12),
    .out13(demultiplexer_1_out13), .out14(demultiplexer_1_out14), .out15(demultiplexer_1_out15),
    .out16(demultiplexer_1_out16), .out17(demultiplexer_1_out17), .out18(demultiplexer_1_out18),
    .out19(demultiplexer_1_out19), .out20(demultiplexer_1_out20), .out21(demultiplexer_1_out21),
    .out22(demultiplexer_1_out22), .out23(demultiplexer_1_out23), .out24(demultiplexer_1_out24),
    .out25(demultiplexer_1_out25), .out26(demultiplexer_1_out26), .out27(demultiplexer_1_out27),
    .out28(demultiplexer_1_out28), .out29(demultiplexer_1_out29), .out30(demultiplexer_1_out30),
    .out31(demultiplexer_1_out31), .in(RegWEn), .sel(WriteIndex));  // open: out0
  Register #(.width(32)) register_9 (
    .D(WriteData), .en(demultiplexer_1_out3), .clk(clock_9_out), .Q(register_9_q));  // open: clr
  Clock clock_9 (.out(clock_9_out));
  Register #(.width(32)) register_10 (
    .D(WriteData), .en(demultiplexer_1_out4), .clk(clock_10_out), .Q(register_10_q));  // open: clr
  Clock clock_10 (.out(clock_10_out));
  Register #(.width(32)) register_11 (
    .D(WriteData), .en(demultiplexer_1_out11), .clk(clock_11_out), .Q(register_11_q));  // open: clr
  Clock clock_11 (.out(clock_11_out));
  Register #(.width(32)) register_12 (
    .D(WriteData), .en(demultiplexer_1_out12), .clk(clock_12_out), .Q(register_12_q));  // open: clr
  Clock clock_12 (.out(clock_12_out));
  Register #(.width(32)) register_13 (
    .D(WriteData), .en(demultiplexer_1_out13), .clk(clock_13_out), .Q(register_13_q));  // open: clr
  Clock clock_13 (.out(clock_13_out));
  Register #(.width(32)) register_14 (
    .D(WriteData), .en(demultiplexer_1_out14), .clk(clock_14_out), .Q(register_14_q));  // open: clr
  Clock clock_14 (.out(clock_14_out));
  Register #(.width(32)) register_15 (
    .D(WriteData), .en(demultiplexer_1_out15), .clk(clock_15_out), .Q(register_15_q));  // open: clr
  Clock clock_15 (.out(clock_15_out));
  Register #(.width(32)) register_16 (
    .D(WriteData), .en(demultiplexer_1_out16), .clk(clock_16_out), .Q(register_16_q));  // open: clr
  Clock clock_16 (.out(clock_16_out));
  Register #(.width(32)) register_17 (
    .D(WriteData), .en(demultiplexer_1_out17), .clk(clock_17_out), .Q(register_17_q));  // open: clr
  Clock clock_17 (.out(clock_17_out));
  Register #(.width(32)) register_18 (
    .D(WriteData), .en(demultiplexer_1_out18), .clk(clock_18_out), .Q(register_18_q));  // open: clr
  Clock clock_18 (.out(clock_18_out));
  Register #(.width(32)) register_19 (
    .D(WriteData), .en(demultiplexer_1_out19), .clk(clock_19_out), .Q(register_19_q));  // open: clr
  Clock clock_19 (.out(clock_19_out));
  Register #(.width(32)) register_20 (
    .D(WriteData), .en(demultiplexer_1_out20), .clk(clock_20_out), .Q(register_20_q));  // open: clr
  Clock clock_20 (.out(clock_20_out));
  Register #(.width(32)) register_21 (
    .D(WriteData), .en(demultiplexer_1_out21), .clk(clock_21_out), .Q(register_21_q));  // open: clr
  Clock clock_21 (.out(clock_21_out));
  Register #(.width(32)) register_22 (
    .D(WriteData), .en(demultiplexer_1_out22), .clk(clock_22_out), .Q(register_22_q));  // open: clr
  Clock clock_22 (.out(clock_22_out));
  Register #(.width(32)) register_23 (
    .D(WriteData), .en(demultiplexer_1_out23), .clk(clock_23_out), .Q(register_23_q));  // open: clr
  Clock clock_23 (.out(clock_23_out));
  Register #(.width(32)) register_24 (
    .D(WriteData), .en(demultiplexer_1_out24), .clk(clock_24_out), .Q(register_24_q));  // open: clr
  Clock clock_24 (.out(clock_24_out));
  Register #(.width(32)) register_25 (
    .D(WriteData), .en(demultiplexer_1_out25), .clk(clock_25_out), .Q(register_25_q));  // open: clr
  Clock clock_25 (.out(clock_25_out));
  Register #(.width(32)) register_26 (
    .D(WriteData), .en(demultiplexer_1_out26), .clk(clock_26_out), .Q(register_26_q));  // open: clr
  Clock clock_26 (.out(clock_26_out));
  Register #(.width(32)) register_27 (
    .D(WriteData), .en(demultiplexer_1_out27), .clk(clock_27_out), .Q(register_27_q));  // open: clr
  Clock clock_27 (.out(clock_27_out));
  Register #(.width(32)) register_28 (
    .D(WriteData), .en(demultiplexer_1_out28), .clk(clock_28_out), .Q(register_28_q));  // open: clr
  Clock clock_28 (.out(clock_28_out));
  Register #(.width(32)) register_29 (
    .D(WriteData), .en(demultiplexer_1_out29), .clk(clock_29_out), .Q(register_29_q));  // open: clr
  Clock clock_29 (.out(clock_29_out));
  Register #(.width(32)) register_30 (
    .D(WriteData), .en(demultiplexer_1_out30), .clk(clock_30_out), .Q(register_30_q));  // open: clr
  Clock clock_30 (.out(clock_30_out));
  Register #(.width(32)) register_31 (
    .D(WriteData), .en(demultiplexer_1_out31), .clk(clock_31_out), .Q(register_31_q));  // open: clr
  Clock clock_31 (.out(clock_31_out));
  Multiplexer #(.select(5), .width(32)) multiplexer_1 (
    .in0({32{1'b0}}), .in1(ra), .in2(sp), .in3(register_9_q), .in4(register_10_q), .in5(t0), .in6(t1),
    .in7(t2), .in8(s0), .in9(s1), .in10(a0), .in11(register_11_q), .in12(register_12_q),
    .in13(register_13_q), .in14(register_14_q), .in15(register_15_q), .in16(register_16_q),
    .in17(register_17_q), .in18(register_18_q), .in19(register_19_q), .in20(register_20_q),
    .in21(register_21_q), .in22(register_22_q), .in23(register_23_q), .in24(register_24_q),
    .in25(register_25_q), .in26(register_26_q), .in27(register_27_q), .in28(register_28_q),
    .in29(register_29_q), .in30(register_30_q), .in31(register_31_q), .out(ReadData1), .sel(ReadIndex1));
  Multiplexer #(.select(5), .width(32)) multiplexer_2 (
    .in0({32{1'b0}}), .in1(ra), .in2(sp), .in3(register_9_q), .in4(register_10_q), .in5(t0), .in6(t1),
    .in7(t2), .in8(s0), .in9(s1), .in10(a0), .in11(register_11_q), .in12(register_12_q),
    .in13(register_13_q), .in14(register_14_q), .in15(register_15_q), .in16(register_16_q),
    .in17(register_17_q), .in18(register_18_q), .in19(register_19_q), .in20(register_20_q),
    .in21(register_21_q), .in22(register_22_q), .in23(register_23_q), .in24(register_24_q),
    .in25(register_25_q), .in26(register_26_q), .in27(register_27_q), .in28(register_28_q),
    .in29(register_29_q), .in30(register_30_q), .in31(register_31_q), .out(ReadData2), .sel(ReadIndex2));

  // Notes on the sheet:
  //   INPUTS to your circuit
  //   DON'T CHANGE THE LOCATIONS OF THE INPUTS AND OUTPUTS!
  //   These are DEBUG/TEST outputs from your circuit.
  //   OUTPUTS from your circuit
endmodule
